# Fritzing sketch schematic (saved by Fritzing 0.7.10b)

parts:
  R11 = Trimmer Potentiometer [maximum_resistance=10kΩ package=THT]
  Reset = Pushbutton [package=THT]
  AUX = male pin header, 3 pins [form="♂ (male)"]
  Reset_2 = male pin header, 2 pins [form="♂ (male)"]
  J9 = female pin header, 3 pins [form="♀ (female)"]
  D1 = Rectifier Diode [part_number=1N4001 package="300 mil [THT]"]
  J13 = female pin header, 6 pins [form="♀ (female)"]
  R3 = Resistor [tolerance=±5% resistance=10k package=THT]
  R9 = Trimmer Potentiometer [maximum_resistance=10kΩ package=THT]
  Sensors = male pin header, 6 pins [form="♂ (male)"]
  J8 = female pin header, 3 pins [form="♀ (female)"]
  R4 = Photocell (LDR) [package=THT]
  C4 = Electrolytic Capacitor [capacitance=10µF voltage=16V package="100 mil [THT, electrolytic]"]
  U3 = Voltage Regulator - 5V [package="TO220 [THT]"]
  ISP = double row male pin header, 6 pins [form="♂ (male)"]
  R8 = Trimmer Potentiometer [maximum_resistance=10kΩ package=THT]
  Base_Motor = Basic Servo
  C1 = Ceramic Capacitor [capacitance=100nF package="100 mil [THT, multilayer]"]
  Base_Motor_2 = male pin header, 3 pins [form="♂ (male)"]
  J11 = female pin header, 2 pins [form="♀ (female)"]
  XTAL1 = Crystal [frequency="16 Mhz" package=THT]
  U2 = atmega328 [package=dip]
  Sensor_Motor = Basic Servo
  C2 = Ceramic Capacitor [capacitance=100nF package="100 mil [THT, multilayer]"]
  6VDC = Screw terminal - 2 pins [package=THT]
  R6 = Photocell (LDR) [package=THT]
  J5 = female pin header, 3 pins [form="♀ (female)"]
  Diagnostic_Input = Rotary Potentiometer (Small) [maximum_resistance=100kΩ]
  R10 = Trimmer Potentiometer [maximum_resistance=10kΩ package=THT]
  R7 = Photocell (LDR) [package=THT]
  Sensor_Motor_2 = male pin header, 3 pins [form="♂ (male)"]
  C3 = Electrolytic Capacitor [capacitance=22µF voltage=16V package="200 mil [THT, electrolytic]"]
  R5 = Photocell (LDR) [package=THT]

nets:
  N1: R11.wiper, Sensors.pin4, U2.A4
  GND: R11.leg2, AUX.pin3, Reset_2.pin2, R9.leg2, C4.-, U3.GND, ISP.pin6, R8.leg2, C1.0, Base_Motor_2.pin3, U2.GND, C2.0, 6VDC.pin2, R10.leg2, Sensor_Motor_2.pin3, C3.-
  N2: Reset.leg0, J11.pin1
  N3: Reset.leg1, J11.pin2
  N4: AUX.pin1, U2.A1
  5V: AUX.pin2, R3.Pin_0, Sensors.pin1, Sensors.pin2, ISP.pin2, U2.VCC, U2.AVCC, U2.AREF
  Reset: Reset_2.pin1, R3.Pin_1, ISP.pin4, U2.RESET
  N5: J9.pin1, Sensor_Motor.pulse
  N6: J9.pin2, Sensor_Motor.vcc
  N7: J9.pin3, Sensor_Motor.gnd
  N8: D1.cathode, Base_Motor_2.pin2, Sensor_Motor_2.pin2
  6V: D1.anode, U3.input_voltage, 6VDC.pin1, C3.+
  N9: J13.pin1, R6.pin_1, R7.pin_1
  N10: J13.pin2, R4.pin_1, R5.pin_1
  N11: J13.pin3, R7.pin_0
  N12: J13.pin4, R6.pin_0
  N13: J13.pin5, R5.pin_0
  N14: J13.pin6, R4.pin_0
  N15: R9.wiper, Sensors.pin3, U2.A5
  N16: Sensors.pin5, U2.A3, R10.wiper
  N17: Sensors.pin6, R8.wiper, U2.A2
  N18: J8.pin1, Base_Motor.pulse
  N19: J8.pin2, Base_Motor.vcc
  N20: J8.pin3, Base_Motor.gnd
  N21: C4.+, U3.output_voltage
  MISO: ISP.pin1, U2.D12
  SCK: ISP.pin3, U2.D13
  net label: ISP.pin5
  N22: C1.1, XTAL1.pin_0, U2.XLAT1
  N23: Base_Motor_2.pin1, U2.D10_(PWM)
  N24: XTAL1.pin_1, U2.XLAT2, C2.1
  N25: U2.D9_(PWM), Sensor_Motor_2.pin1
  MOSI: U2.D11_(PWM)
  N26: J5.pin1, Diagnostic_Input.wiper
  N27: J5.pin2, Diagnostic_Input.leg1
  N28: J5.pin3, Diagnostic_Input.leg2
